# Fritzing sketch ESP control board - 3 (saved by Fritzing 1.0.3b)
perfboards: 1

parts:
  Header_Subwoofer = female pin header, 7 pins [form="♀ (female)"]
  Series_resistor = Resistor [tolerance=±5% resistance=10k power=0.25W package=THT]
  NPN = NPN-Transistor [part_number=BC547B package="TO92 [THT]"]
  ESP32-WROOM32 = LuaNode32 / ESP32 [part_number=ESP32S-PIN30]
  Pull_Up = Resistor [tolerance=±5% power=0.25W resistance=100k package=THT]
  Bauteil2 = I2C level shifter bidirectional
  NPN1 = NPN-Transistor [part_number=BC547B package="TO92 [THT]"]
  Series_resistor_MUTE = Resistor [tolerance=±5% resistance=10k power=0.25W package=THT]

nets:
  N1: Header_Subwoofer.pin1, ESP32-WROOM32.Vin, Pull_Up.Pin_1, Bauteil2.HV, NPN1.C
  GND: Header_Subwoofer.pin2, NPN.E, ESP32-WROOM32.GND, Bauteil2.GND
  N2: Header_Subwoofer.pin3, NPN.C, Pull_Up.Pin_0
  N3: Header_Subwoofer.pin4, NPN1.E
  N4: Header_Subwoofer.pin5, Bauteil2.HV3
  N5: Header_Subwoofer.pin6, Bauteil2.HV4
  N6: Header_Subwoofer.pin7, Bauteil2.HV2
  N7: Series_resistor.Pin_0, NPN.B
  N8: Series_resistor.Pin_1, ESP32-WROOM32.D18
  N9: ESP32-WROOM32.3V3, Bauteil2.LV
  N10: ESP32-WROOM32.TX2, Bauteil2.LV2
  N11: ESP32-WROOM32.D19, Series_resistor_MUTE.Pin_1
  N12: ESP32-WROOM32.D21, Bauteil2.LV4
  N13: ESP32-WROOM32.D22, Bauteil2.LV3
  N14: NPN1.B, Series_resistor_MUTE.Pin_0

notes:
  ST und MUTE getauscht!
  solder
  Draht Kupfer Seite
  Draht Komponenten Seite

custom parts:
  LuaNode32 / ESP32: New Image for LuaNode32 DOIT ESP32 DEVKIT V1. Base parts from LuaNode32 / ESP32 ESP32 based LuaNode32 by G.Noorlander DOIT Esp32 DevKit v1 (30 pins long, 11 pins width) by Werner Rothschopf (modified by vanepp Dec 2018)
